// Logisim project nélio_junior-01_09_2022.circ as structural Verilog: 9 circuits, main circuit main
module main (
  input  [3:0] in_1,
  input  [3:0] in_2,
  input  [2:0] in_3,
  output [3:0] out_4
);

  wire decoder_1_out0, decoder_1_out1, decoder_1_out2, decoder_1_out3, decoder_1_out4, decoder_1_out5,
       decoder_1_out6;
  wire [3:0] and_1_out_3, nand_1_out_3, nor_1_out_3, not_1_out_2, nxor_1_out_3, or_1_out_3, xor_1_out_3;

  Decoder #(.select(3)) decoder_1 (
    .out0(decoder_1_out0), .out1(decoder_1_out1), .out2(decoder_1_out2), .out3(decoder_1_out3),
    .out4(decoder_1_out4), .out5(decoder_1_out5), .out6(decoder_1_out6), .sel(in_3));  // open: out7, en
  AND and_1 (.out_3(and_1_out_3), .in_1(in_2), .in_2(in_1));
  assign out_4 = decoder_1_out0 ? and_1_out_3 : 4'bz;  // Controlled_Buffer controlled_buffer_1
  OR or_1 (.out_3(or_1_out_3), .in_1(in_2), .in_2(in_1));
  assign out_4 = decoder_1_out1 ? or_1_out_3 : 4'bz;  // Controlled_Buffer controlled_buffer_2
  XOR xor_1 (.out_3(xor_1_out_3), .in_1(in_2), .in_2(in_1));
  assign out_4 = decoder_1_out2 ? xor_1_out_3 : 4'bz;  // Controlled_Buffer controlled_buffer_3
  NAND nand_1 (.out_3(nand_1_out_3), .in_1(in_2), .in_2(in_1));
  assign out_4 = decoder_1_out3 ? nand_1_out_3 : 4'bz;  // Controlled_Buffer controlled_buffer_4
  NOR nor_1 (.out_3(nor_1_out_3), .in_1(in_2), .in_2(in_1));
  assign out_4 = decoder_1_out4 ? nor_1_out_3 : 4'bz;  // Controlled_Buffer controlled_buffer_5
  NXOR nxor_1 (.out_3(nxor_1_out_3), .in_1(in_2), .in_2(in_1));
  assign out_4 = decoder_1_out5 ? nxor_1_out_3 : 4'bz;  // Controlled_Buffer controlled_buffer_6
  NOT not_1 (.out_2(not_1_out_2), .in_1(in_2));
  assign out_4 = decoder_1_out6 ? not_1_out_2 : 4'bz;  // Controlled_Buffer controlled_buffer_7
endmodule

module AND (
  input  [3:0] in_1,
  input  [3:0] in_2,
  output [3:0] out_3
);

  and and_1 (out_3[1], in_1[1], in_2[1]);
  and and_2 (out_3[0], in_1[0], in_2[0]);
  and and_3 (out_3[2], in_1[2], in_2[2]);
  and and_4 (out_3[3], in_1[3], in_2[3]);
endmodule

module OR (
  input  [3:0] in_1,
  input  [3:0] in_2,
  output [3:0] out_3
);

  or or_1 (out_3[1], in_1[1], in_2[1]);
  or or_2 (out_3[0], in_1[0], in_2[0]);
  or or_3 (out_3[2], in_1[2], in_2[2]);
  or or_4 (out_3[3], in_1[3], in_2[3]);
endmodule

module XOR (
  input  [3:0] in_1,
  input  [3:0] in_2,
  output [3:0] out_3
);

  xor xor_1 (out_3[0], in_1[0], in_2[0]);
  xor xor_2 (out_3[1], in_1[1], in_2[1]);
  xor xor_3 (out_3[2], in_1[2], in_2[2]);
  xor xor_4 (out_3[3], in_1[3], in_2[3]);
endmodule

module NAND (
  input  [3:0] in_1,
  input  [3:0] in_2,
  output [3:0] out_3
);

  nand nand_1 (out_3[0], in_1[0], in_2[0]);
  nand nand_2 (out_3[1], in_1[1], in_2[1]);
  nand nand_3 (out_3[2], in_1[2], in_2[2]);
  nand nand_4 (out_3[3], in_1[3], in_2[3]);
endmodule

module NOR (
  input  [3:0] in_1,
  input  [3:0] in_2,
  output [3:0] out_3
);

  nor nor_1 (out_3[0], in_1[0], in_2[0]);
  nor nor_2 (out_3[1], in_1[1], in_2[1]);
  nor nor_3 (out_3[2], in_1[2], in_2[2]);
  nor nor_4 (out_3[3], in_1[3], in_2[3]);
endmodule

module NXOR (
  input  [3:0] in_1,
  input  [3:0] in_2,
  output [3:0] out_3
);

  xnor xnor_1 (out_3[1], in_1[1], in_2[1]);
  xnor xnor_2 (out_3[0], in_1[0], in_2[0]);
  xnor xnor_3 (out_3[2], in_1[2], in_2[2]);
  xnor xnor_4 (out_3[3], in_1[3], in_2[3]);
endmodule

module NOT (
  input  [3:0] in_1,
  output [3:0] out_2
);

  assign out_2 = ~in_1;  // NOT_Gate not_1, 4 bits wide
endmodule

module ula (
  input  [3:0] in_1,
  input  [3:0] in_2,
  input  [2:0] in_3,
  output [3:0] out_4
);

  wire decoder_1_out0, decoder_1_out1, decoder_1_out2, decoder_1_out3, decoder_1_out4, decoder_1_out5,
       decoder_1_out6;
  wire [3:0] and_1_out, nand_1_out, nor_1_out, not_1_out, or_1_out, xnor_1_out, xor_1_out;

  Decoder #(.select(3)) decoder_1 (
    .out0(decoder_1_out0), .out1(decoder_1_out1), .out2(decoder_1_out2), .out3(decoder_1_out3),
    .out4(decoder_1_out4), .out5(decoder_1_out5), .out6(decoder_1_out6), .sel(in_3));  // open: out7, en
  assign and_1_out = in_2 & in_1;  // AND_Gate and_1, 4 bits wide
  assign out_4 = decoder_1_out0 ? and_1_out : 4'bz;  // Controlled_Buffer controlled_buffer_1
  assign or_1_out = in_2 | in_1;  // OR_Gate or_1, 4 bits wide
  assign out_4 = decoder_1_out1 ? or_1_out : 4'bz;  // Controlled_Buffer controlled_buffer_2
  assign xor_1_out = in_2 ^ in_1;  // XOR_Gate xor_1, 4 bits wide
  assign out_4 = decoder_1_out2 ? xor_1_out : 4'bz;  // Controlled_Buffer controlled_buffer_3
  assign nand_1_out = ~(in_2 & in_1);  // NAND_Gate nand_1, 4 bits wide
  assign out_4 = decoder_1_out3 ? nand_1_out : 4'bz;  // Controlled_Buffer controlled_buffer_4
  assign nor_1_out = ~(in_2 | in_1);  // NOR_Gate nor_1, 4 bits wide
  assign out_4 = decoder_1_out4 ? nor_1_out : 4'bz;  // Controlled_Buffer controlled_buffer_5
  assign xnor_1_out = ~(in_2 ^ in_1);  // XNOR_Gate xnor_1, 4 bits wide
  assign out_4 = decoder_1_out5 ? xnor_1_out : 4'bz;  // Controlled_Buffer controlled_buffer_6
  assign not_1_out = ~in_2;  // NOT_Gate not_1, 4 bits wide
  assign out_4 = decoder_1_out6 ? not_1_out : 4'bz;  // Controlled_Buffer controlled_buffer_7
endmodule
